# Fritzing sketch ESP32-LED-Strips (saved by Fritzing 0.9.3b)
breadboards: 1

parts:
  RE1 = KY-040 Rotary encoder [package=THT]
  MH-ET_Live_Minikit_for_ESP1 = MH-ET Live Minikit for ESP32
  WS = Round Pushbutton
  BAT1 = Battery Holders [package=battcon_245mm]
  RT = Round Pushbutton
  J4 = Screw terminal - 2 pins [package=THT]
  J5 = Screw terminal - 2 pins [package=THT]
  T2 = Screw terminal - 2 pins [package=THT]
  CLK/DT = Screw terminal - 2 pins [package=THT]
  SW/+ = Screw terminal - 2 pins [package=THT]
  J11 = Screw terminal - 2 pins [package=THT]
  GND = Screw terminal - 2 pins [package=THT]
  JP1 = Header 4 [package=screwterminal-3.5mm-4_lock]
  LED1_R = Basic FET N-Channel [package="TO220 [THT]"]
  R1 = Resistor [tolerance=±5% resistance=100 package="2010 [SMD]"]
  LED1_G = Basic FET N-Channel [package="TO220 [THT]"]
  LED1_B = Basic FET N-Channel [package="TO220 [THT]"]
  LED1 = RGB LED - (4 legs) [package="5 mm [THT]"]
  R2 = Resistor [tolerance=±5% resistance=100 package="2010 [SMD]"]
  R3 = Resistor [tolerance=±5% resistance=100 package="2010 [SMD]"]
  R4 = Resistor [tolerance=±5% resistance=100 package="2010 [SMD]"]
  T1 = screw terminal, 2 pins
  J13 = Screw terminal - 2 pins [package=THT]
  J17 = Screw terminal - 2 pins [package=THT]
  LED1_G1 = Basic FET N-Channel [package="TO220 [THT]"]
  LED1_R1 = Basic FET N-Channel [package="TO220 [THT]"]
  LED1_B1 = Basic FET N-Channel [package="TO220 [THT]"]
  R5 = Resistor [tolerance=±5% resistance=100 package="2010 [SMD]"]
  R6 = Resistor [tolerance=±5% resistance=100 package="2010 [SMD]"]
  R7 = Resistor [tolerance=±5% resistance=100 package="2010 [SMD]"]
  R8 = Resistor [tolerance=±5% resistance=100 package="2010 [SMD]"]
  LED2 = RGB LED - (4 legs) [package="5 mm [THT]"]
  J18 = Screw terminal - 2 pins [package=THT]
  J19 = Screw terminal - 2 pins [package=THT]
  LED1_B2 = Basic FET N-Channel [package="TO220 [THT]"]
  LED1_G2 = Basic FET N-Channel [package="TO220 [THT]"]
  LED1_R2 = Basic FET N-Channel [package="TO220 [THT]"]
  R9 = Resistor [tolerance=±5% resistance=100 package="2010 [SMD]"]
  R10 = Resistor [tolerance=±5% resistance=100 package="2010 [SMD]"]
  R11 = Resistor [tolerance=±5% resistance=100 package="2010 [SMD]"]
  R12 = Resistor [tolerance=±5% resistance=100 package="2010 [SMD]"]
  LED3 = RGB LED - (4 legs) [package="5 mm [THT]"]

nets:
  GND: RE1.GND, MH-ET_Live_Minikit_for_ESP1.GND, BAT1.-, J11.pin2, GND.pin2, JP1.2
  VCC: RE1.Vcc, MH-ET_Live_Minikit_for_ESP1.VCC, WS.leg1, RT.leg1, T2.pin2, SW/+.pin1, JP1.1, T1.pin2
  N1: RE1.SW, MH-ET_Live_Minikit_for_ESP1.TMS, SW/+.pin2
  N2: RE1.DT, MH-ET_Live_Minikit_for_ESP1.IO34, CLK/DT.pin1
  N3: RE1.CLK, MH-ET_Live_Minikit_for_ESP1.IO33, CLK/DT.pin2
  N4: MH-ET_Live_Minikit_for_ESP1.SVN, WS.leg0, T1.pin1
  N5: MH-ET_Live_Minikit_for_ESP1.IO35, RT.leg0, T2.pin1
  N6: MH-ET_Live_Minikit_for_ESP1.IO26, R9.Pin_0
  N7: MH-ET_Live_Minikit_for_ESP1.IO18, R12.Pin_0
  N8: MH-ET_Live_Minikit_for_ESP1.IO19, R11.Pin_0
  N9: MH-ET_Live_Minikit_for_ESP1.IO22, R5.Pin_0
  N10: MH-ET_Live_Minikit_for_ESP1.IO21, R7.Pin_0
  N11: MH-ET_Live_Minikit_for_ESP1.IO17, R8.Pin_0
  N12: MH-ET_Live_Minikit_for_ESP1.IO27, R1.Pin_0
  N13: MH-ET_Live_Minikit_for_ESP1.IO25, R2.Pin_0
  N14: MH-ET_Live_Minikit_for_ESP1.IO32, R3.Pin_0
  N15: BAT1.+, J4.pin1, J11.pin1, JP1.3, LED1.common_anode, J17.pin1, LED2.common_anode, J19.pin1, LED3.common_anode
  N16: J4.pin2, LED1_R.source, LED1.red_cathode
  N17: J5.pin1, LED1_G.source, LED1.green_cathode
  N18: J5.pin2, LED1_B.source, LED1.blue_cathode
  N19: LED1_R.gate, R1.Pin_1, R4.Pin_0
  N20: LED1_R.drain, R4.Pin_1
  N21: LED1_G.gate, R2.Pin_1
  N22: LED1_B.gate, R3.Pin_1
  N23: J13.pin1, LED1_G1.source, LED2.green_cathode
  N24: J13.pin2, LED1_B1.source, LED2.blue_cathode
  N25: J17.pin2, LED1_R1.source, LED2.red_cathode
  N26: LED1_G1.gate, R7.Pin_1
  N27: LED1_R1.gate, R5.Pin_1, R6.Pin_0
  N28: LED1_R1.drain, R6.Pin_1
  N29: LED1_B1.gate, R8.Pin_1
  N30: J18.pin1, LED1_G2.source, LED3.green_cathode
  N31: J18.pin2, LED1_B2.source, LED3.blue_cathode
  N32: J19.pin2, LED1_R2.source, LED3.red_cathode
  N33: LED1_B2.gate, R11.Pin_1
  N34: LED1_G2.gate, R12.Pin_1
  N35: LED1_R2.gate, R9.Pin_1, R10.Pin_0
  N36: LED1_R2.drain, R10.Pin_1

custom parts:
  KY-040 Rotary encoder: KY-040 Rotary Encoder with switch on breakout borad from AZ Delivery
  MH-ET Live Minikit for ESP32: MH-ET Live Minikit for ESP32 ( http://mh.nodebb.com/topic/8/mh-et-live-minikit-for-esp32/2/) PCB footprint is invalid.
